// Logisim project cpu.circ as structural Verilog: 15 circuits, main circuit main
module main (
  input  Rst
);

  wire alu_1_c, alu_1_z, and_1_out, Clk_out, dipswitch_1_p1, HLT, jsd_1_weo, not_1_out, sr_1_fo;
  wire [1:0] undriven_4;
  wire [7:0] alu_1_ao, ar_1_adho, ar_1_adlo, dp_1_adho, dp_1_adlo, memory_1_do;
  wire [10:0] undriven_2;
  wire [11:0] undriven;
  wire [13:0] undriven_3;

  Clock Clk (.out(Clk_out));
  LED u_Hlt (.in(HLT));
  not not_1 (not_1_out, HLT);
  and and_1 (and_1_out, Clk_out, not_1_out);
  IR ir_1 (.WE(dipswitch_1_p1), .DI(memory_1_do), .Clk(and_1_out), .Reset(Rst));  // open: DO
  // DipSwitch #(.number(10)) dipswitch_1: pin names not known; wires that end beside it: dipswitch_1_p1
  // DipSwitch #(.number(10)) dipswitch_2: pin names not known
  // DipSwitch #(.number(10)) dipswitch_3: pin names not known
  // DipSwitch #(.number(10)) dipswitch_4: pin names not known
  // DipSwitch #(.number(10)) dipswitch_5: pin names not known
  Memory memory_1 (
    .DO(memory_1_do), .WE(undriven_4[1]), .Clk(and_1_out), .DI(memory_1_do), .ADL(dp_1_adlo),
    .ADH(dp_1_adho), .OE(undriven_4[0]));
  // Probe on undriven_2[6:3]
  ALU alu_1 (
    .AO(alu_1_ao), .C(alu_1_c), .Z(alu_1_z), .AOE(undriven_2[7]), .DBI(memory_1_do), .AI(alu_1_ao),
    .OpS(undriven_2[6:3]));  // open: RO
  // Probe on memory_1_do
  R r_1 (
    .out_8(memory_1_do), .DBI(memory_1_do), .RWE(undriven_2[2]), .DWE(undriven_2[0]), .Clk(and_1_out),
    .Rst(Rst), .OE(undriven_2[1]));  // open: RI
  LED led_1 (.in(alu_1_c));
  LED led_2 (.in(alu_1_z));
  A a_1 (
    .DBO(memory_1_do), .RO(alu_1_ao), .DBI(memory_1_do), .RI(alu_1_ao), .RWE(undriven_2[7]),
    .DWE(undriven_2[8]), .Clk(and_1_out), .Rst(Rst), .ROE(undriven_2[9]), .DOE(undriven_2[10]));
  DP dp_1 (
    .ADLO(dp_1_adlo), .ADHO(dp_1_adho), .ADLI(ar_1_adlo), .ADHI(ar_1_adho), .WE(undriven[0]),
    .Clk(and_1_out), .Rst(Rst));
  AR ar_1 (
    .ADLO(ar_1_adlo), .ADHO(ar_1_adho), .LWE(undriven[1]), .HWE(undriven[2]), .ADLI(memory_1_do),
    .Clk(and_1_out), .Rst(Rst), .OE(undriven[3]));
  PC pc_1 (
    .ABLO(ar_1_adlo), .ABHO(ar_1_adho), .DB(memory_1_do), .Reset(Rst), .ABWE(jsd_1_weo), .CE(undriven[5]),
    .Clk(and_1_out), .ABLI(ar_1_adlo), .ABHI(ar_1_adho), .AOE(undriven[6]), .LOE(undriven[7]),
    .HOE(undriven[8]));
  XY xy_1 (
    .DBO(memory_1_do), .XWE(undriven_3[5]), .YWE(undriven_3[7]), .DBI(memory_1_do), .Clk(and_1_out),
    .Reset(Rst), .XOE(undriven_3[6]), .YOE(undriven_3[8]));
  // Probe on ar_1_adlo
  Latch latch_1 (
    .DBO(memory_1_do), .ADLO(ar_1_adlo), .ADHO(ar_1_adho), .DBI(memory_1_do), .CL(undriven[10]),
    .CH(undriven[11]), .ADLI(ar_1_adlo), .ADHI(ar_1_adho));
  SP sp_1 (
    .AHO(ar_1_adho), .ALO(ar_1_adlo), .DO(memory_1_do), .DI(memory_1_do), .WE(undriven_3[2]),
    .IE(undriven_3[0]), .Clk(and_1_out), .DE(undriven_3[1]), .Rst(Rst), .AOE(undriven_3[4]),
    .DOE(undriven_3[3]));
  // Probe on ar_1_adho
  JSD jsd_1 (.WEO(jsd_1_weo), .WEI(undriven[4]), .JE(sr_1_fo), .Inv(undriven[9]));
  SR sr_1 (
    .FO(sr_1_fo), .HO(HLT), .DO(memory_1_do), .OE(undriven_3[10]), .WE(undriven_3[9]), .DI(memory_1_do),
    .Clk(and_1_out), .Rst(Rst), .FS(undriven_3[13:11]));  // open: IO
  // Probe on undriven_3[13:11]

  // Notes on the sheet:
  //   1-10
  //   11-20
  //   21-30
  //   31-40
  //   41-
endmodule

module PC (
  input  Reset,
  input  ABWE,
  input  CE,
  input  Clk,
  input  AOE,
  input  [7:0] ABLI,
  input  [7:0] ABHI,
  input  LOE,
  input  HOE,
  output [7:0] ABLO,
  output [7:0] ABHO,
  output [7:0] DB
);

  wire or_1_out;
  wire [7:0] multiplexer_1_out;
  wire [15:0] counter_1_q;

  Counter #(.max('hffff), .width(16)) counter_1 (
    .clr(Reset), .load(ABWE), .up(1'b1), .count(CE), .clk(Clk), .D({ABHI, ABLI}), .Q(counter_1_q));  // open: carry
  assign {ABHO, ABLO} = AOE ? counter_1_q : 16'bz;  // Controlled_Buffer controlled_buffer_1
  or or_1 (or_1_out, HOE, LOE);
  Multiplexer #(.width(8)) multiplexer_1 (
    .in0(counter_1_q[7:0]), .in1(counter_1_q[15:8]), .out(multiplexer_1_out), .sel(HOE));
  assign DB = or_1_out ? multiplexer_1_out : 8'bz;  // Controlled_Buffer controlled_buffer_2
endmodule

module Memory (
  input  WE,
  input  Clk,
  input  [7:0] DI,
  input  OE,
  input  [7:0] ADL,
  input  [7:0] ADH,
  output [7:0] DO
);

  wire and_1_out, not_1_out, not_2_out;
  wire [7:0] controlled_buffer_1_out, ram_1_dout, rom_1_data;

  not not_1 (not_1_out, ADH[7]);
  RAM #(.addrWidth(15)) ram_1 (
    .addr({ADH[6:0], ADL}), .we(and_1_out), .oe(1'b1), .clk(Clk), .din(DI), .dout(ram_1_dout));
  and and_1 (and_1_out, WE, not_1_out);
  ROM #(.addrWidth(15)) rom_1 (.addr({ADH[6:0], ADL}), .data(rom_1_data));
  assign controlled_buffer_1_out = not_2_out ? ram_1_dout : 8'bz;  // Controlled_Buffer controlled_buffer_1
  not not_2 (not_2_out, ADH[7]);
  assign DO = OE ? controlled_buffer_1_out : 8'bz;  // Controlled_Buffer controlled_buffer_2
  assign controlled_buffer_1_out = ADH[7] ? rom_1_data : 8'bz;  // Controlled_Buffer controlled_buffer_3
endmodule

module XY (
  input  Clk,
  input  Reset,
  input  [7:0] DBI,
  input  XOE,
  input  XWE,
  input  YOE,
  input  YWE,
  output [7:0] DBO
);

  wire [7:0] register_1_q, register_2_q;

  Register register_1 (.D(DBI), .en(XWE), .clk(Clk), .Q(register_1_q), .clr(Reset));
  Register register_2 (.D(DBI), .en(YWE), .clk(Clk), .Q(register_2_q), .clr(Reset));
  assign DBO = XOE ? register_1_q : 8'bz;  // Controlled_Buffer controlled_buffer_1
  assign DBO = YOE ? register_2_q : 8'bz;  // Controlled_Buffer controlled_buffer_2
endmodule

module CSD (
  input  [7:0] Opcode,
  output PCE,
  output PCI,
  output PCO,
  output LAI,
  output LAO,
  output HAI,
  output HAO,
  output SPI,
  output SPO,
  output MEI,
  output MEO,
  output IRI,
  output ARI,
  output ARO,
  output XRI,
  output XRO,
  output YRI,
  output YRO,
  output SRI,
  output SRO,
  output RFI,
  output CFI,
  output IFS,
  output IFC,
  output HFS,
  output ZFO,
  output CFO,
  output EFO,
  output LFO,
  output GFO,
  output IFO,
  output AAD,
  output ASU,
  output AMU,
  output ADI,
  output AAN,
  output AIO,
  output AXO,
  output ASL,
  output ASR,
  output ANO,
  output AIN,
  output ADE,
  output ALO
);

  wire [47:44] rom_1_data;

  ROM #(.dataWidth(48)) rom_1 (
    .addr(Opcode),
    .data({rom_1_data, ALO, ADE, AIN, ANO, ASR, ASL, AXO, AIO, AAN, ADI, AMU, ASU, AAD, IFO, GFO, LFO, EFO, CFO, ZFO, HFS, IFC, IFS, CFI, RFI, SRO, SRI, YRO, YRI, XRO, XRI, ARO, ARI, IRI, MEO, MEI, SPO, SPI, HAO, HAI, LAO, LAI, PCO, PCI, PCE}));
endmodule

module ALU (
  input  [3:0] OpS,
  input  [7:0] DBI,
  input  AOE,
  input  [7:0] AI,
  output [7:0] RO,
  output [7:0] AO,
  output C,
  output Z
);

  wire adder_1_cout, adder_2_cout, and_1_out, and_2_out, demultiplexer_1_out1, demultiplexer_1_out2,
       demultiplexer_1_out3, demultiplexer_1_out4, demultiplexer_1_out5, demultiplexer_1_out6,
       demultiplexer_1_out7, demultiplexer_1_out8, demultiplexer_1_out9, demultiplexer_1_out10,
       demultiplexer_1_out11, demultiplexer_1_out12, subtractor_1_bout, subtractor_2_bout;
  wire [7:0] adder_1_out, adder_2_out, and_3_out, divider_1_out, divider_1_rem, multiplier_1_cout,
       multiplier_1_out, not_1_out, or_1_out, shifter_1_out, shifter_2_out, subtractor_1_out,
       subtractor_2_out, xor_1_out;

  assign RO = demultiplexer_1_out1 ? adder_1_out : 8'bz;  // Controlled_Buffer controlled_buffer_1
  Adder adder_1 (.a(AI), .b(DBI), .out(adder_1_out), .cout(adder_1_cout));  // open: cin
  assign C = demultiplexer_1_out1 ? adder_1_cout : 1'bz;  // Controlled_Buffer controlled_buffer_2
  assign RO = demultiplexer_1_out2 ? subtractor_1_out : 8'bz;  // Controlled_Buffer controlled_buffer_3
  Subtractor subtractor_1 (.a(AI), .b(DBI), .out(subtractor_1_out), .bout(subtractor_1_bout));  // open: bin
  assign C = demultiplexer_1_out2 ? subtractor_1_bout : 1'bz;  // Controlled_Buffer controlled_buffer_4
  assign RO = demultiplexer_1_out3 ? multiplier_1_out : 8'bz;  // Controlled_Buffer controlled_buffer_5
  Multiplier multiplier_1 (.a(AI), .b(DBI), .out(multiplier_1_out), .cout(multiplier_1_cout));  // open: cin
  assign RO = demultiplexer_1_out4 ? divider_1_out : 8'bz;  // Controlled_Buffer controlled_buffer_6
  Divider divider_1 (.a(AI), .b(DBI), .out(divider_1_out), .rem(divider_1_rem));  // open: upper
  Demultiplexer #(.select(4)) demultiplexer_1 (
    .out1(demultiplexer_1_out1), .out2(demultiplexer_1_out2), .out3(demultiplexer_1_out3),
    .out4(demultiplexer_1_out4), .out5(demultiplexer_1_out5), .out6(demultiplexer_1_out6),
    .out7(demultiplexer_1_out7), .out8(demultiplexer_1_out8), .out9(demultiplexer_1_out9),
    .out10(demultiplexer_1_out10), .out11(demultiplexer_1_out11), .out12(demultiplexer_1_out12), .in(1'b1),
    .sel(OpS));  // open: out0, out13, out14, out15
  and and_1 (and_1_out, multiplier_1_cout[0], multiplier_1_cout[1], multiplier_1_cout[2], multiplier_1_cout[3], multiplier_1_cout[4], multiplier_1_cout[5], multiplier_1_cout[6], multiplier_1_cout[7]);
  assign C = demultiplexer_1_out3 ? and_1_out : 1'bz;  // Controlled_Buffer controlled_buffer_7
  and and_2 (and_2_out, divider_1_rem[0], divider_1_rem[1], divider_1_rem[2], divider_1_rem[3], divider_1_rem[4], divider_1_rem[5], divider_1_rem[6], divider_1_rem[7]);
  assign C = demultiplexer_1_out4 ? and_2_out : 1'bz;  // Controlled_Buffer controlled_buffer_8
  assign and_3_out = AI & DBI;  // AND_Gate and_3, 8 bits wide
  assign RO = demultiplexer_1_out5 ? and_3_out : 8'bz;  // Controlled_Buffer controlled_buffer_9
  assign or_1_out = AI | DBI;  // OR_Gate or_1, 8 bits wide
  assign RO = demultiplexer_1_out6 ? or_1_out : 8'bz;  // Controlled_Buffer controlled_buffer_10
  assign xor_1_out = AI ^ DBI;  // XOR_Gate xor_1, 8 bits wide
  assign RO = demultiplexer_1_out7 ? xor_1_out : 8'bz;  // Controlled_Buffer controlled_buffer_11
  assign RO = demultiplexer_1_out8 ? shifter_1_out : 8'bz;  // Controlled_Buffer controlled_buffer_12
  Shifter shifter_1 (.in(AI), .\dist (DBI[2:0]), .out(shifter_1_out));
  assign RO = demultiplexer_1_out9 ? shifter_2_out : 8'bz;  // Controlled_Buffer controlled_buffer_13
  Shifter #(.shift("lr")) shifter_2 (.in(AI), .\dist (DBI[2:0]), .out(shifter_2_out));
  assign not_1_out = ~DBI;  // NOT_Gate not_1, 8 bits wide
  assign RO = demultiplexer_1_out10 ? not_1_out : 8'bz;  // Controlled_Buffer controlled_buffer_14
  assign RO = demultiplexer_1_out11 ? adder_2_out : 8'bz;  // Controlled_Buffer controlled_buffer_15
  Adder adder_2 (.a(DBI), .b(8'h1), .out(adder_2_out), .cin(1'b0), .cout(adder_2_cout));
  assign C = demultiplexer_1_out11 ? adder_2_cout : 1'bz;  // Controlled_Buffer controlled_buffer_16
  assign RO = demultiplexer_1_out12 ? subtractor_2_out : 8'bz;  // Controlled_Buffer controlled_buffer_17
  Subtractor subtractor_2 (.a(DBI), .b(8'h1), .out(subtractor_2_out), .bin(1'b0), .bout(subtractor_2_bout));
  assign C = demultiplexer_1_out12 ? subtractor_2_bout : 1'bz;  // Controlled_Buffer controlled_buffer_18
  Pull_Resistor pull_resistor_1 (.node(RO));
  assign AO = AOE ? RO : 8'bz;  // Controlled_Buffer controlled_buffer_19
  Pull_Resistor pull_resistor_2 (.node(C));
  nor nor_1 (Z, RO[0], RO[1], RO[2], RO[3], RO[4], RO[5], RO[6], RO[7]);
endmodule

module IR (
  input  [7:0] DI,
  input  WE,
  input  Clk,
  input  Reset,
  output [7:0] DO
);

  Register register_1 (.D(DI), .en(WE), .clk(Clk), .Q(DO), .clr(Reset));
endmodule

module AR (
  input  Clk,
  input  Rst,
  input  OE,
  input  [7:0] ADLI,
  input  LWE,
  input  HWE,
  output [7:0] ADLO,
  output [7:0] ADHO
);

  wire [7:0] register_1_q, register_2_q;

  Register register_1 (.D(ADLI), .en(LWE), .clk(Clk), .Q(register_1_q), .clr(Rst));
  Register register_2 (.D(ADLI), .en(HWE), .clk(Clk), .Q(register_2_q), .clr(Rst));
  assign ADLO = OE ? register_1_q : 8'bz;  // Controlled_Buffer controlled_buffer_1
  assign ADHO = OE ? register_2_q : 8'bz;  // Controlled_Buffer controlled_buffer_2
endmodule

module DP (
  input  Clk,
  input  Rst,
  input  [7:0] ADLI,
  input  [7:0] ADHI,
  input  WE,
  output [7:0] ADLO,
  output [7:0] ADHO
);

  Register #(.width(16)) register_1 (.D({ADHI, ADLI}), .en(WE), .clk(Clk), .Q({ADHO, ADLO}), .clr(Rst));
endmodule

module SP (
  input  IE,
  input  DE,
  input  AOE,
  input  [7:0] DI,
  input  DOE,
  input  WE,
  input  Clk,
  input  Rst,
  output [7:0] AHO,
  output [7:0] ALO,
  output [7:0] DO
);

  wire not_1_out, xor_1_out;
  wire [7:0] counter_1_q;

  not not_1 (not_1_out, DE);
  xor xor_1 (xor_1_out, IE, DE);
  Counter counter_1 (
    .load(WE), .D(DI), .count(xor_1_out), .Q(counter_1_q), .up(not_1_out), .clk(Clk), .clr(Rst));  // open: carry
  assign AHO = AOE ? 8'h1 : 8'bz;  // Controlled_Buffer controlled_buffer_1
  assign ALO = AOE ? counter_1_q : 8'bz;  // Controlled_Buffer controlled_buffer_2
  assign DO = DOE ? counter_1_q : 8'bz;  // Controlled_Buffer controlled_buffer_3
endmodule

module JSD (
  input  WEI,
  input  JE,
  input  Inv,
  output WEO
);

  wire multiplexer_1_out, not_1_out;

  Multiplexer multiplexer_1 (.in0(JE), .in1(not_1_out), .out(multiplexer_1_out), .sel(Inv));
  Pull_Resistor #(.pull(1)) pull_resistor_1 (.node(multiplexer_1_out));
  not not_1 (not_1_out, JE);
  and and_1 (WEO, WEI, multiplexer_1_out);
endmodule

module SR (
  input  [2:0] FS,
  input  OE,
  input  [7:0] DI,
  input  WE,
  input  Clk,
  input  Rst,
  output [7:0] DO,
  output FO,
  output IO,
  output HO
);

  wire demultiplexer_1_out0, demultiplexer_1_out1, demultiplexer_1_out2, demultiplexer_1_out3,
       demultiplexer_1_out4;
  wire [5:0] register_1_q;

  Register register_1 (.D(DI), .en(WE), .clk(Clk), .Q({HO, IO, register_1_q}), .clr(Rst));
  Demultiplexer #(.select(3)) demultiplexer_1 (
    .out0(demultiplexer_1_out0), .out1(demultiplexer_1_out1), .out2(demultiplexer_1_out2),
    .out3(demultiplexer_1_out3), .out4(demultiplexer_1_out4), .in(1'b1), .sel(FS));  // open: out5, out6, out7
  assign FO = demultiplexer_1_out0 ? register_1_q[0] : 1'bz;  // Controlled_Buffer controlled_buffer_1
  assign FO = demultiplexer_1_out1 ? register_1_q[1] : 1'bz;  // Controlled_Buffer controlled_buffer_2
  assign FO = demultiplexer_1_out2 ? register_1_q[2] : 1'bz;  // Controlled_Buffer controlled_buffer_3
  assign FO = demultiplexer_1_out3 ? register_1_q[3] : 1'bz;  // Controlled_Buffer controlled_buffer_4
  assign DO = OE ? {HO, IO, register_1_q} : 8'bz;  // Controlled_Buffer controlled_buffer_5
  assign FO = demultiplexer_1_out4 ? register_1_q[4] : 1'bz;  // Controlled_Buffer controlled_buffer_6
endmodule

module Latch (
  input  CL,
  input  CH,
  input  [7:0] ADLI,
  input  [7:0] DBI,
  input  [7:0] ADHI,
  output [7:0] ADLO,
  output [7:0] DBO,
  output [7:0] ADHO
);

  assign ADLO = CL ? DBI : 8'bz;  // Controlled_Buffer controlled_buffer_1
  assign DBO = CL ? ADLI : 8'bz;  // Controlled_Buffer controlled_buffer_2
  assign DBO = CH ? ADHI : 8'bz;  // Controlled_Buffer controlled_buffer_3
  assign ADHO = CH ? DBI : 8'bz;  // Controlled_Buffer controlled_buffer_4
endmodule

module R (
  input  RWE,
  input  DWE,
  input  OE,
  input  [7:0] DBI,
  input  [7:0] RI,
  input  Clk,
  input  Rst,
  output [7:0] out_8
);

  wire or_1_out;
  wire [7:0] controlled_buffer_1_out, register_1_q;

  assign controlled_buffer_1_out = RWE ? RI : 8'bz;  // Controlled_Buffer controlled_buffer_1
  or or_1 (or_1_out, DWE, RWE);
  Register register_1 (.D(controlled_buffer_1_out), .en(or_1_out), .clk(Clk), .Q(register_1_q), .clr(Rst));
  assign controlled_buffer_1_out = DWE ? DBI : 8'bz;  // Controlled_Buffer controlled_buffer_2
  assign out_8 = OE ? register_1_q : 8'bz;  // Controlled_Buffer controlled_buffer_3
endmodule

module A (
  input  RWE,
  input  DWE,
  input  ROE,
  input  DOE,
  input  [7:0] DBI,
  input  [7:0] RI,
  input  Clk,
  input  Rst,
  output [7:0] DBO,
  output [7:0] RO
);

  wire or_1_out;
  wire [7:0] controlled_buffer_1_out, register_1_q;

  assign controlled_buffer_1_out = RWE ? RI : 8'bz;  // Controlled_Buffer controlled_buffer_1
  or or_1 (or_1_out, DWE, RWE);
  Register register_1 (.D(controlled_buffer_1_out), .en(or_1_out), .clk(Clk), .Q(register_1_q), .clr(Rst));
  assign controlled_buffer_1_out = DWE ? DBI : 8'bz;  // Controlled_Buffer controlled_buffer_2
  assign DBO = DOE ? register_1_q : 8'bz;  // Controlled_Buffer controlled_buffer_3
  assign RO = ROE ? register_1_q : 8'bz;  // Controlled_Buffer controlled_buffer_4
endmodule
